# Fritzing sketch 7Segment_direct (saved by Fritzing 1.0.3b)
circuit board: 6.88566cm x 5.36311cm
breadboards: 2

parts:
  Digit_4 = 7 Segment Display
  Digit_3 = 7 Segment Display
  Digit_2 = 7 Segment Display
  Digit_1 = 7 Segment Display
  Arduino1 = Arduino Uno (Rev3)

nets:
  N1: Digit_4.Segment_E, Digit_3.Segment_E, Digit_2.Segment_E, Digit_1.Segment_E, Arduino1.D6_PWM
  N2: Digit_4.Segment_D, Digit_3.Segment_D, Digit_2.Segment_D, Digit_1.Segment_D, Arduino1.D5_PWM
  N3: Digit_4.common_anode, Arduino1.D13/SCK
  N4: Digit_4.Segment_C, Digit_3.Segment_C, Digit_2.Segment_C, Digit_1.Segment_C
  N5: Digit_4.Segment_DP, Digit_3.Segment_DP, Digit_2.Segment_DP, Digit_1.Segment_DP, Arduino1.D4
  N6: Digit_4.Segment_B, Digit_3.Segment_B, Digit_2.Segment_B, Digit_1.Segment_B, Arduino1.D3_PWM
  N7: Digit_4.Segment_A, Digit_3.Segment_A, Digit_2.Segment_A, Digit_1.Segment_A, Arduino1.D2
  N8: Digit_4.Segment_F, Digit_3.Segment_F, Digit_2.Segment_F, Digit_1.Segment_F, Arduino1.D7
  N9: Digit_4.Segment_G, Digit_3.Segment_G, Digit_2.Segment_G, Digit_1.Segment_G, Arduino1.D8
  N10: Digit_3.common_anode, Arduino1.D12/MISO
  N11: Digit_2.common_anode, Arduino1.D11_PWM/MOSI
  N12: Digit_1.common_anode, Arduino1.D10_PWM/SS

// code stored in the sketch: 7Segment_direct.ino
/*

Easy way to control 7 segment displays by Arduino

Stefan Hermann
www.fritzing.org


         _________           _________           _________           _________
        /____a____\         /____a____\         /____a____\         /____a____\
       | |       | |       | |       | |       | |       | |       | |       | | 
       |f|       |b|       |f|       |b|       |f|       |b|       |f|       |b|
       | |       | |       | |       | |       | |       | |       | |       | |       
       \_/_______\_/       \_/_______\_/       \_/_______\_/       \_/_______\_/
        _|___g___|_         _|___g___|_         _|___g___|_         _|___g___|_ 
       / \       / \       / \       / \       / \       / \       / \       / \
       | |       | |       | |       | |       | |       | |       | |       | |
       |e|       |c|       |e|       |c|       |e|       |c|       |e|       |c|
       \_/_______\_/ __    \_/_______\_/ __    \_/_______\_/ __    \_/_______\_/ __
        \____d____/ |DP|    \____d____/ |DP|    \____d____/ |DP|    \____d____/ |DP|
  
         Digit 4             Digit 3             Digit 2             Digit 1            
*/

const int numberOfSegments = 8;                            // do not change
int segmentPins[numberOfSegments] = {2,3,4,5,6,7,8,9};     // change to your pins a,b,c,d,e,f,g,DP
  
const int numberOfDigits = 4;                              // change to the number of digits
int commonPins[numberOfDigits] = {13,12,11,10};            // change to the pins of digits starting with the left digit

int displayType=1;                                         // change to the type of your display: common anode = 1; common cathode = 2;

int myNumber=0;

int theFigures[11][7]={
{1,1,1,1,1,1,0},
{0,1,1,0,0,0,0},
{1,1,0,1,1,0,1},
{1,1,1,1,0,0,1},
{0,1,1,0,0,1,1},
{1,0,1,1,0,1,1},
{1,0,1,1,1,1,1},
{1,1,1,0,0,0,0},
{1,1,1,1,1,1,1},
{1,1,1,0,0,1,1},
{0,0,0,0,0,0,1}};

void setup(){  
  // config for the display
  for (int i=0; i<numberOfSegments;i++){
    pinMode(segmentPins[i],OUTPUT);
  }
  
  for (int i=0; i<numberOfDigits;i++){
    pinMode(commonPins[i],OUTPUT);
  }
  
  // type your setup code here
  
}

void loop(){
  // type in your loop code here
  
  // this is just for the example:
  showNumber(myNumber);        // display the number
  if (  myNumber++;
  delay(1);

}

// do not change the methods below

void showNumber(int theNumber){
  for (int stelle=numberOfDigits; stelle>=0; stelle--){
    char szZahl[numberOfDigits];
    sprintf(szZahl, "%d", theNumber);
    int stellen = strlen(szZahl);
    if (stelle > stellen) {
      
    } else {
      int ergebnis = szZahl[stelle] - '0';
      if (ergebnis>-1){
        digit(((numberOfDigits-1)-(stellen-(stelle+1))),ergebnis);
      } 
      else {
        digit(((numberOfDigits-1)-(stellen-(stelle+1))),0);
      }
    }
    delay(1);
    clearDisplay();
  }
}



void digit(int theDigit, int theNumber){
  if (displayType==1){
    digitalWrite(commonPins[theDigit], HIGH);
      for (int i=0; i<7; i++){
      if (theFigures[theNumber][i]==0){
        digitalWrite(segmentPins[i],HIGH);
      } else {
        digitalWrite(segmentPins[i],LOW);
      }
    }
  } else {
    digitalWrite(commonPins[theDigit], LOW);
    for (int i=0; i<7; i++){
      digitalWrite(segmentPins[i],theFigures[theNumber][i]);    
    }

  }  
}

void clearDisplay(){
  for (int theDigit=0; theDigit<numberOfDigits;theDigit++){
  if (displayType==1){
    digitalWrite(commonPins[theDigit], LOW);
      for (int i=0; i<7; i++){
        digitalWrite(segmentPins[i],HIGH);     
    }
  } else {
    digitalWrite(commonPins[theDigit], HIGH);
    for (int i=0; i<7; i++){
        digitalWrite(segmentPins[i],LOW);
    }
  }  
  }
}
