# Fritzing sketch Matrix (saved by Fritzing 1.0.3b)
circuit board: 8.93198cm x 6.1522cm
breadboards: 2

parts:
  Disp2 = LBT2088AH [part_number=LBT2088AH]
  R5 = Resistor [tolerance=±5% resistance=220 power=0.25W package=THT]
  R6 = Resistor [tolerance=±5% resistance=220 power=0.25W package=THT]
  R7 = Resistor [tolerance=±5% resistance=220 power=0.25W package=THT]
  R8 = Resistor [tolerance=±5% resistance=220 power=0.25W package=THT]
  R9 = Resistor [tolerance=±5% resistance=220 power=0.25W package=THT]
  R10 = Resistor [tolerance=±5% resistance=220 power=0.25W package=THT]
  R11 = Resistor [tolerance=±5% resistance=220 power=0.25W package=THT]
  R12 = Resistor [tolerance=±5% resistance=220 power=0.25W package=THT]
  Arduino1 = Arduino Uno (Rev3)

nets:
  N1: Disp2.pin1, R9.Pin_1
  N2: Disp2.pin2, R11.Pin_1
  N3: Disp2.pin_3, Arduino1.D3_PWM
  N4: Disp2.pin_4, Arduino1.D2
  N5: Disp2.pin_5, R12.Pin_1
  N6: Disp2.pin_6, Arduino1.A1
  N7: Disp2.pin_7, R10.Pin_1
  N8: Disp2.pin_8, R7.Pin_1
  N9: Disp2.pin_9, R5.Pin_1
  N10: Disp2.pin_10, Arduino1.D12/MISO
  N11: Disp2.pin_11, Arduino1.D11_PWM/MOSI
  N12: Disp2.pin_12, R6.Pin_1
  N13: Disp2.pin_13, Arduino1.D9_PWM
  N14: Disp2.pin_14, R8.Pin_1
  N15: Disp2.pin_15, Arduino1.D7
  N16: Disp2.pin_16, Arduino1.D6_PWM
  N17: R5.Pin_0, Arduino1.D13/SCK
  N18: R6.Pin_0, Arduino1.D10_PWM/SS
  N19: R7.Pin_0, Arduino1.A3
  N20: R8.Pin_0, Arduino1.D8
  N21: R9.Pin_0, Arduino1.D5_PWM
  N22: R10.Pin_0, Arduino1.A2
  N23: R11.Pin_0, Arduino1.D4
  N24: R12.Pin_0, Arduino1.A0

notes:
  MATRIX

custom parts:
  LBT2088AH: LED Matrix Display 8x8 red 60.5mm

// code stored in the sketch: Matrix.ino
/*
  Matrix
  LED-Matrix displaying image
  
  This example is part of the Fritzing Creator Kit: www.fritzing.org/creator-kit.
*/

// pin order for Arduino UNO
int rowPins[8] = {9,3,2,12,15,11,7,6};      // matrix rows connected to the Arduino
int colPins[8] = {13,8,17,10,5,16,4,14};   // matrix columns connected to the Arduino


// pin order for Arduino MEGA
// int rowPins[8] = {9,3,2,12,55,11,7,6};       // matrix rows connected to the Arduino
// int colPins[8] = {13,8,57,10,5,56,4,54};    // matrix columns connected to the Arduino

int image[8][8]={                               // the image displayed on the matrix : 1 = LED on, 0 = LED off
  
{0,1,0,0,0,0,1,0},  
{1,1,1,0,0,1,1,1},
{0,1,0,0,0,0,1,0},
{0,0,0,1,1,0,0,0},
{0,0,0,1,1,0,0,0},
{1,0,0,0,0,0,0,1},
{0,1,1,1,1,1,1,0},
{0,0,1,1,1,1,0,0}

};                                              

void setup(){
  for (int i=0; i<8; i++){                       // all pins are declared as outputs 
    pinMode(rowPins[i],OUTPUT);
    pinMode(colPins[i],OUTPUT);
  }
}

void loop(){
  for (int y=0; y<8; y++){                       // rowwise 
    for (int x=0; x<8; x++){                     // check all entries of the array from left to right 
      if (image[x][y]==1){                       // is the entry 1
        digitalWrite(colPins[x],HIGH);           // switch on column pin
      } else {                                   // else
        digitalWrite(colPins[x],LOW);            // switch it off
      }
    }
    digitalWrite(rowPins[y],LOW);                // switch the row pin to LOW (because it is the cathode of the LED; LOW means ON)
    delayMicroseconds(100);                      // stop the program for 100 milliseconds
    digitalWrite(rowPins[y],HIGH);               // switch the row pin to HIGH (this means OFF)
  }
}
