# Fritzing sketch PingPong (saved by Fritzing 1.0.3b)
circuit board: 9.8137cm x 6.23953cm
breadboards: 2

parts:
  Disp2 = LBT2088AH [part_number=LBT2088AH]
  R5 = Resistor [tolerance=±5% resistance=220 power=0.25W package=THT]
  R6 = Resistor [tolerance=±5% resistance=220 power=0.25W package=THT]
  R7 = Resistor [tolerance=±5% resistance=220 power=0.25W package=THT]
  R8 = Resistor [tolerance=±5% resistance=220 power=0.25W package=THT]
  R9 = Resistor [tolerance=±5% resistance=220 power=0.25W package=THT]
  R10 = Resistor [tolerance=±5% resistance=220 power=0.25W package=THT]
  R11 = Resistor [tolerance=±5% resistance=220 power=0.25W package=THT]
  R12 = Resistor [tolerance=±5% resistance=220 power=0.25W package=THT]
  Arduino1 = Arduino Uno (Rev3)
  R13 = Rotary Potentiometer (Small) [maximum_resistance=10kΩ knob_status=50% power=0.5W package=THT]
  R14 = Rotary Potentiometer (Small) [maximum_resistance=10kΩ knob_status=50% power=0.5W package=THT]

nets:
  N1: Disp2.pin1, R9.Pin_1
  N2: Disp2.pin2, R11.Pin_1
  N3: Disp2.pin_3, Arduino1.D3_PWM
  N4: Disp2.pin_4, Arduino1.D2
  N5: Disp2.pin_5, R12.Pin_1
  N6: Disp2.pin_6, Arduino1.A1
  N7: Disp2.pin_7, R10.Pin_1
  N8: Disp2.pin_8, R7.Pin_1
  N9: Disp2.pin_9, R5.Pin_1
  N10: Disp2.pin_10, Arduino1.D12/MISO
  N11: Disp2.pin_11, Arduino1.D11_PWM/MOSI
  N12: Disp2.pin_12, R6.Pin_1
  N13: Disp2.pin_13, Arduino1.D9_PWM
  N14: Disp2.pin_14, R8.Pin_1
  N15: Disp2.pin_15, Arduino1.D7
  N16: Disp2.pin_16, Arduino1.D6_PWM
  N17: R5.Pin_0, Arduino1.D13/SCK
  N18: R6.Pin_0, Arduino1.D10_PWM/SS
  N19: R7.Pin_0, Arduino1.A3
  N20: R8.Pin_0, Arduino1.D8
  N21: R9.Pin_0, Arduino1.D5_PWM
  N22: R10.Pin_0, Arduino1.A2
  N23: R11.Pin_0, Arduino1.D4
  N24: R12.Pin_0, Arduino1.A0
  N25: Arduino1.A4/SDA, R13.wiper
  N26: Arduino1.A5/SCL, R14.wiper
  GND: Arduino1.GND, R13.leg2, R14.leg1
  5V: Arduino1.5V, R13.leg1, R14.leg2

notes:
  PING_PONG

custom parts:
  LBT2088AH: LED Matrix Display 8x8 red 60.5mm

// code stored in the sketch: PingPong.ino
/*
  Ping Pong game
  LED-Matrix is used to play Ping Pong
  
  This example is part of the Fritzing Creator Kit: www.fritzing.org/creator-kit.
*/

// pin order for Arduino UNO
int rowPins[8] = {9,3,2,12,15,11,7,6};      // matrix rows connected to the Arduino
int colPins[8] = {13,8,17,10,5,16,4,14};   // matrix columns connected to the Arduino


// pin order for Arduino MEGA
// int rowPins[8] = {9,3,2,12,55,11,7,6};       // matrix rows connected to the Arduino
// int colPins[8] = {13,8,57,10,5,56,4,54};    // matrix columns connected to the Arduino

int pot1Pin=18;                                // declaring the pin for player 1's potentiometer
int pot2Pin=19;                                // declaring the pin for player 2's potentiometer

int image[8][8]={                              // clear 
{0,0,0,0,0,0,0,0},  
{0,0,0,0,0,0,0,0},
{0,0,0,0,0,0,0,0},
{0,0,0,0,0,0,0,0},
{0,0,0,0,0,0,0,0},
{0,0,0,0,0,0,0,0},
{0,0,0,0,0,0,0,0},
{0,0,0,0,0,0,0,0}
};                                              

int death[8][8]={                              // all on
{1,1,1,1,1,1,1,1},  
{1,1,1,1,1,1,1,1}, 
{1,1,1,1,1,1,1,1}, 
{1,1,1,1,1,1,1,1}, 
{1,1,1,1,1,1,1,1},  
{1,1,1,1,1,1,1,1}, 
{1,1,1,1,1,1,1,1}, 
{1,1,1,1,1,1,1,1}
};   

int death2[8][8]={                             // skull
{0,1,1,1,1,1,0,0},  
{1,1,1,1,1,1,1,0},
{1,0,0,1,0,0,1,0},
{1,1,1,1,1,1,1,0},
{0,1,1,1,1,1,0,0},
{0,1,0,1,0,1,0,0},
{0,1,0,1,0,1,0,0},
{0,0,0,0,0,0,0,0}
};   

int blank[8][8]={                              // all off
{0,0,0,0,0,0,0,0},  
{0,0,0,0,0,0,0,0},
{0,0,0,0,0,0,0,0},
{0,0,0,0,0,0,0,0},
{0,0,0,0,0,0,0,0},
{0,0,0,0,0,0,0,0},
{0,0,0,0,0,0,0,0},
{0,0,0,0,0,0,0,0}
};    

long theTimer;                                           // timer variable

int gameState=0;                                         // storing the game status
int animations=300;                                      // storing the duration of the images between the games

float ballXSpeed = 1;                                    // storing the x acceleration   
float ballXPosition=4;                                   // storing the ball position as number

float ballYSpeed = 0;                                    // storing the y acceleration
float ballYPosition=4;                                   // storing the ball position as number

int imageYPosition;                                      // storing the image position as number
int imageXPosition;                                      // storing the image position as number

int player1Position=3;                                   // storing the paddle positoin of player 1
int player2Position=3;                                   // storing the paddle positoin of player 2

int gameSpeed;                                           // storing the current game speed

void setup(){
  for (int i=0; i<8; i++){                               // all pins are outputs
    pinMode(rowPins[i],OUTPUT);
    pinMode(colPins[i],OUTPUT);
  }
}

void draw(){
  for (int y=0; y<8; y++){                               // rowwise 
    for (int x=0; x<8; x++){                             // from left to right, entries are checked
      if (image[x][y]==1){                               // if entry equals 1
        digitalWrite(colPins[x],HIGH);                   // the column pin is switched on
      } else {                                           // else
        digitalWrite(colPins[x],LOW);                    // the column pin is switched off
      } 
    }
    digitalWrite(rowPins[y],LOW);                        // switch the row pin to LOW (because it is the cathod of the LED LOW menas ON)
    delayMicroseconds(1000);                             // stop the program for 1 seconds
    digitalWrite(rowPins[y],HIGH);                       // switch the row pin to HIGH (what means OFF)
  }
}

void update(){
  switch (gameState) {                                   // switching game mode (called state machine)
  case 0:                                                // new game
    memcpy(image,blank,sizeof(blank));                   // clear screen
    gameSpeed=300;                                       // set the game speed
    ballXPosition=3;                                     // set ball position
    ballYPosition=3;                                     // set ball position
    ballYSpeed=0;                                        // ball should fly straight
    if (random(0,2)>0){                                  // but randomly left or right
      ballXSpeed=1;
    } else {
      ballXSpeed=-1;
    }     
    theTimer=millis(); 
    gameState=1;
    break;
  case 1:                                                // game active
    image[player1Position][0]=0;                         // paddle player 1 clear old position
    image[player1Position+1][0]=0;                       // paddle player 1 clear old position
    image[player2Position][7]=0;                         // paddle player 2 clear old position
    image[player2Position+1][7]=0;                       // paddle player 2 clear old position

    player1Position=map(analogRead(pot1Pin),0,1023,0,6); // reading the position of player 1
    player2Position=map(analogRead(pot2Pin),0,1023,0,6); // reading the position of player 2
    
    image[player1Position][0]=1;                         // paddle player 1 display             
    image[player1Position+1][0]=1;                       // paddle player 1 display
    image[player2Position][7]=1;                         // paddle player 2 display
    image[player2Position+1][7]=1;                       // paddle player 2 display
  
    if (millis()>theTimer+gameSpeed){                    // timer for game speed
      if (gameSpeed>50) gameSpeed-=3;                    // accelerate game
      theTimer=millis();                                 // set new timer
      image[imageYPosition][imageXPosition]=0;           // overwrite old position
      ballXPosition+=ballXSpeed;                         // update position
      ballYPosition+=ballYSpeed;                         // update position      
      
      if (ballYPosition>=7) ballYSpeed*=-1;              // collision bottom border
      if (ballYPosition<=0) ballYSpeed*=-1;              // collision top border

      ballYPosition=constrain(ballYPosition,0,7);        // constrain values between 0 and 7
      ballXPosition=constrain(ballXPosition,0,7);        // constrain values between 0 and 7
      imageYPosition=round(ballYPosition);                
      imageXPosition=round(ballXPosition);      
      
      if ((ballXPosition>=6)&&(image[imageYPosition][7]==1)) {  // if ball hits a paddle
        ballXSpeed*=-1;                                    // reflect the ball
        ballYSpeed=random(-2,3);                           // random reflection angle
      }
      if ((ballXPosition<=1)&&(image[imageYPosition][0]==1)) {  // if ball hits a paddle
        ballXSpeed*=-1;                                    // reflect the ball
        ballYSpeed=random(-2,3);                           // random reflection angle
      }
      if (ballXPosition>=7){                               // ball out
        gameState=2;                                       // change status to lost game
        theTimer=millis();                                 // new timer is set
      }

      if (ballXPosition<=0){                               // ball out
        gameState=2;                                       // change status to lost game
        theTimer=millis();                                 // new timer is set
      }

      image[imageYPosition][imageXPosition]=1;             // set new image position
      
    }
    break;  
  case 2:                                                  // game was lost
    if (millis()>theTimer+gameSpeed){                      // wait for a short time
      theTimer=millis();
      gameState=3;                                         // game state to lost game display
    }
    break;
  case 3:                                                  // lost game display
    memcpy(image,death,sizeof(death));                     // show image of lost game, memcpy is a function copying one array to another
    if (millis()>theTimer+animations){                     // wait again
      gameState=0;                                         // game state change to »start a game«
    }
    break;
  }
}

void loop(){
  update();                                                // all calculations are in the update method
  draw();                                                  // all display methods are in here
}
