# Fritzing sketch full_wave_rectifier (saved by Fritzing 1.0.3b)
breadboards: 1

parts:
  U1 = Transformer [Lin=9 Lout=100 Rin=1Ω Rout=1Ω input_inductance=40 output_inductance=10H input_resistance=1Ω output_resistance=1Ω package=transformer]
  Oscilloscope1 = Oscilloscope [volts/div=1V time/div=10ms ch1_offset=0V ch2_offset=0V ch3_offset=0V ch4_offset=0V ch1_volts/div=5V ch2_volts/div=5V ch3_volts/div=5V ch4_volts/div=5V horizontal_position=0s]
  V1 = AC Power [voltage=5V amplitude=20 frequency=60Hz offset_voltage=0V delay_time=0s damping_factor=0s-1 phase=0degrees internal_resistance=0.1Ω]
  Oscilloscope2 = Oscilloscope [volts/div=1V time/div=10ms ch1_offset=0V ch2_offset=0V ch3_offset=0V ch4_offset=0V ch1_volts/div=5V ch2_volts/div=5V ch3_volts/div=5V ch4_volts/div=5V horizontal_position=0s]
  R1 = Resistor [tolerance=±5% power=0.25W resistance=1G package=THT]
  R2 = Resistor [tolerance=±5% power=0.25W resistance=220 package=THT]  # not connected
  C1 = Electrolytic Capacitor [capacitance=1mF voltage=50V package="100 mil [THT, electrolytic]"]
  R3 = Resistor [tolerance=±5% power=4W resistance=100 package=THT]
  S2 = Pushbutton [package=THT]
  D4 = Schottky Diode [part_number=1N5817 package="300 mil [THT]"]
  D1 = Schottky Diode [part_number=1N5817 package="300 mil [THT]"]
  D2 = Schottky Diode [part_number=1N5817 package="300 mil [THT]"]
  D3 = Schottky Diode [part_number=1N5817 package="300 mil [THT]"]
  D5 = Schottky Diode [part_number=1N5817 package="300 mil [THT]"]
  S1 = Pushbutton [package=THT]

nets:
  voltage_source+: U1.1, Oscilloscope1.V1_Probe, V1.V+, Oscilloscope2.V1_Probe
  voltage_source-: U1.2, V1.V-, Oscilloscope2.COM_Probe, R1.Pin_0
  N1: U1.3, D2.anode, D3.cathode
  secondary+: U1.4, Oscilloscope1.V2_Probe, Oscilloscope2.V2_Probe, S1.leg0
  GND: Oscilloscope1.COM_Probe, R1.Pin_1, C1.-, R3.Pin_1, D4.anode, D3.anode
  rectified: Oscilloscope1.V3_Probe, Oscilloscope2.V3_Probe, D1.cathode, D2.cathode, D5.anode
  load: Oscilloscope1.V4_Probe, R3.Pin_0, S2.leg0, D5.cathode
  N2: C1.+, S2.leg1
  N3: D4.cathode, D1.anode, S1.leg1
