# Fritzing sketch Timer (saved by Fritzing 1.0.3b)
circuit board: 6.88566cm x 5.36311cm
breadboards: 2

parts:
  7_Segment1 = 7 Segment Display
  S2 = Pushbutton [package="[THT]"]
  S1 = Pushbutton [package="[THT]"]
  R2 = Resistor [resistance=10k tolerance=±5% power=0.25W package=THT]
  7_Segment2 = 7 Segment Display
  R30 = Resistor [resistance=220 tolerance=±5% power=0.25W package=THT]
  R31 = Resistor [resistance=220 tolerance=±5% power=0.25W package=THT]
  R32 = Resistor [resistance=220 tolerance=±5% power=0.25W package=THT]
  R36 = Resistor [resistance=220 tolerance=±5% power=0.25W package=THT]
  R37 = Resistor [resistance=220 tolerance=±5% power=0.25W package=THT]
  R38 = Resistor [resistance=220 tolerance=±5% power=0.25W package=THT]
  R39 = Resistor [resistance=220 tolerance=±5% power=0.25W package=THT]
  R40 = Resistor [resistance=220 tolerance=±5% power=0.25W package=THT]
  R41 = Resistor [resistance=220 tolerance=±5% power=0.25W package=THT]
  R42 = Resistor [resistance=220 tolerance=±5% power=0.25W package=THT]
  R43 = Resistor [resistance=220 tolerance=±5% power=0.25W package=THT]
  R44 = Resistor [resistance=220 tolerance=±5% power=0.25W package=THT]
  R45 = Resistor [resistance=220 tolerance=±5% power=0.25W package=THT]
  R46 = Resistor [resistance=220 tolerance=±5% power=0.25W package=THT]
  R1 = Resistor [resistance=10k tolerance=±5% power=0.25W package=THT]
  IC1 = IC, DIP package, 16 pins [chip_label=595]
  IC2 = IC, DIP package, 16 pins [chip_label=595]
  Arduino1 = Arduino Uno (Rev3)

nets:
  N1: 7_Segment1.Segment_E, R45.Pin_1
  N2: 7_Segment1.Segment_D, R42.Pin_0
  N3: 7_Segment1.common_anode, S2.Pin_3, S2.Pin_4, S1.Pin_3, S1.Pin_4, 7_Segment2.common_anode, IC1.pin10, IC1.pin16, IC2.pin10, IC2.pin16, Arduino1.5V
  N4: 7_Segment1.Segment_C, R41.Pin_0
  N5: 7_Segment1.Segment_B, R40.Pin_0
  N6: 7_Segment1.Segment_A, R43.Pin_0
  N7: 7_Segment1.Segment_F, R39.Pin_1
  N8: 7_Segment1.Segment_G, R38.Pin_1
  N9: S2.Pin_1, S2.Pin_2, R2.Pin_0, Arduino1.D5_PWM
  N10: S1.Pin_1, S1.Pin_2, R1.Pin_0, Arduino1.D6_PWM
  N11: R2.Pin_1, R1.Pin_1, IC1.pin8, IC1.pin13, IC2.pin8, IC2.pin13, Arduino1.GND
  N12: 7_Segment2.Segment_E, R46.Pin_1
  N13: 7_Segment2.Segment_D, R37.Pin_0
  N14: 7_Segment2.Segment_C, R36.Pin_0
  N15: 7_Segment2.Segment_B, R32.Pin_0
  N16: 7_Segment2.Segment_A, R44.Pin_0
  N17: 7_Segment2.Segment_F, R31.Pin_1
  N18: 7_Segment2.Segment_G, R30.Pin_1
  N19: R30.Pin_0, IC2.pin6
  N20: R31.Pin_0, IC2.pin5
  N21: R32.Pin_1, IC2.pin1
  N22: R36.Pin_1, IC2.pin2
  N23: R37.Pin_1, IC2.pin3
  N24: R38.Pin_0, IC1.pin6
  N25: R39.Pin_0, IC1.pin5
  N26: R40.Pin_1, IC1.pin1
  N27: R41.Pin_1, IC1.pin2
  N28: R42.Pin_1, IC1.pin3
  N29: R43.Pin_1, IC1.pin15
  N30: R44.Pin_1, IC2.pin15
  N31: R45.Pin_0, IC1.pin4
  N32: R46.Pin_0, IC2.pin4
  N33: IC1.pin9, IC2.pin14
  N34: IC1.pin11, IC2.pin11, Arduino1.D12/MISO
  N35: IC1.pin12, IC2.pin12, Arduino1.D8
  N36: IC1.pin14, Arduino1.D11_PWM/MOSI

notes:
  Example from Frerk Popovic
  www.popovic.info

// code stored in the sketch: Timer.ino
/*
Code by Frerk Popovic

*/


// Using the Timer-Interrupt from: http://www.arduino.cc/playground/Main/MsTimer2
#include <MsTimer2.h>
// and the Bounce-Library to debounce http://www.arduino.cc/playground/Code/Bounce
#include <Bounce.h>

// for debugging set to 1 and use the serial monitor:
const int DEBUG = 1;

// shift register:
const int latchPin = 8; 
const int dataPin = 11; 
const int clockPin = 12; 

// Pushbuttons
const int leftButton = 6;
const int rightButton = 5; 

int leftButtonState = 0; // is the left button pushed?
int leftButtonLastState = 0; // what was it's last state?

int rightButtonState = 0; // is the right button pushed?

Bounce bouncerLeft = Bounce(leftButton,50); 
Bounce bouncerRight = Bounce(rightButton,50); 

int seconds = 0;

/*
7-Segment-Display:
 a-7  <-> Q0
 b-6  <-> Q1
 c-4  <-> Q2
 d-2  <-> Q3
 e-1  <-> Q4
 f-9  <-> Q5
 g-10 <-> Q6 
 dp-5 <-> Q7 not used
 
 display of one digit numbers:

 0:   f+e+d+c+b+a = 63
 1:         c+b   = 0*2^7 + 0*2^6 + 0*2^5 + 0*2^4 + 0*2^3 + 1^*2^2 + 1*2^1 +0*2^0 = 00000110b = 6
 2: g+  e+d+  b+a = 91
 3: g+    d+c+b+a = 79
 4: g+f+    c+b   = 102
 5: g+f+  d+c+  a = 109
 6: g+f+e+d+c+  a = 125
 7:         c+b+a = 7
 8: g+f+e+d+c+b+a = 127 
 9: g+f+  d+c+b+a = 111
 
 */
int numbers[10] = {
  63, 6, 91, 79, 102, 109, 125, 7, 127, 111};

// Relais for:
const int pump = 10;
const int solenoid = 13; 

void setup()
{
  if(DEBUG){
    Serial.begin(9600);
  }

  pinMode(latchPin, OUTPUT);
  pinMode(clockPin, OUTPUT);
  pinMode(dataPin, OUTPUT);

  pinMode(leftButton, INPUT);
  pinMode(rightButton, INPUT);

  clearDisplays(); 
  delay(100);
  alleAn(); // LED-Test
  delay(500);
  clearDisplays();
  sayHello();
  clearDisplays(); 
  alleAn(); // LED-Test
  delay(1000);

  MsTimer2::set(1000, zeitLaeuft);  

}

void loop()
{
  // 
  bouncerLeft.update();
  leftButtonState = bouncerLeft.read();
  //leftButtonState = digitalRead(leftButton);

  if(DEBUG && leftButtonState && bouncerLeft.duration() > 100 == 1){
    Serial.print("last and current state of buttons:  ");
    Serial.print(leftButtonLastState);
    Serial.print("   ");
    Serial.println(leftButtonState);
    Serial.println("------------------------------------------------");
  }

  if(leftButtonState == 1 && bouncerLeft.duration() > 100 && leftButtonLastState == 0){
    seconds = 0;
    startClock();
    leftButtonLastState++;
  } 
  else if (leftButtonState == 1 && bouncerLeft.duration() > 100 && leftButtonLastState == 1){
    stopClock();
    leftButtonLastState++;
    seconds = 0;
    startClock();    
  }

  bouncerRight.update();
  if(bouncerRight.read() && bouncerRight.duration() > 100){
    rightButtonState = 1;
  } 
  else {
    rightButtonState = 0;
  }

  if(rightButtonState){
    stopClock();
    leftButtonLastState = 0;
    if(DEBUG){
      Serial.println("Right");
      Serial.print("Last state of left button:  ");
      Serial.println(leftButtonLastState);
      Serial.println("|||||||||||||||||STOP||||||||||||||||||||||||||");
    }
  }
  showTime();

}

void showTime(){

  // if(DEBUG){
  //      Serial.print("Die Einerstelle ist: ");
  //      Serial.println(int(seconds%10), DEC);
  //      Serial.print("Die Zehnerstelle ist: ");
  //      Serial.println(int(seconds/10), DEC);
  //      Serial.println("-----------------------------------");
  //    }  
  zahlAusgeben(int(seconds/10),int(seconds%10));
}



void clearDisplays(){
  digitalWrite(latchPin, LOW);
  shiftOut(dataPin, clockPin, LSBFIRST, 0); 
  shiftOut(dataPin, clockPin, LSBFIRST, 0); 
  digitalWrite(latchPin, HIGH);
}

void alleAn(){
  zahlAusgeben(8,8);
}

void sayHello(){
  int pause = 100;
  for(int a = 0;a<3;a++){
    digitalWrite(latchPin, LOW);
    shiftOut(dataPin, clockPin, MSBFIRST,1);
    digitalWrite(latchPin, HIGH);
    delay(pause); 
    digitalWrite(latchPin, LOW);
    shiftOut(dataPin, clockPin, MSBFIRST,0);
    digitalWrite(latchPin, HIGH);
    delay(pause); 
    for(int i =1;i<4;i++){
      digitalWrite(latchPin, LOW);
      shiftOut(dataPin, clockPin, MSBFIRST,int(0.01+pow(2,i)));
      shiftOut(dataPin, clockPin, MSBFIRST,0);
      digitalWrite(latchPin, HIGH);
      delay(pause); 
    }
    for(int i =3;i<6;i++){
      digitalWrite(latchPin, LOW);
      shiftOut(dataPin, clockPin, MSBFIRST,0);
      shiftOut(dataPin, clockPin, MSBFIRST,int(0.1+pow(2,i)));
      digitalWrite(latchPin, HIGH);
      delay(pause); 
    }
    clearDisplays();  
    }
  }

  void zahlAusgeben(int zehner, int einer){
    digitalWrite(latchPin, LOW);
    shiftOut(dataPin, clockPin, MSBFIRST, numbers[einer]); 
    shiftOut(dataPin, clockPin, MSBFIRST, numbers[zehner]);
    digitalWrite(latchPin, HIGH);
  }

void startClock(){
  MsTimer2::start(); // enable Interrupt
  if(DEBUG) Serial.println("Timer started!");
}

void stopClock(){
  MsTimer2::stop(); // disable Interrupt
  if(DEBUG) Serial.println("Timer stopped!");
}


void zeitLaeuft(){
  seconds++;
  if(DEBUG){
    Serial.println("+++++++++++++++Time:+++++++++++++++++");
    Serial.println(seconds);
  }
}
